// Logisim project RIPPLE_CARRY_ADDER.circ as structural Verilog
module HALF_ADDER (
  input  A,
  input  B,
  output SUM,
  output CARRY
);

  xor XOR (SUM, A, B);
  and AND (CARRY, A, B);

  // Notes on the sheet:
  //   HALF ADDER
endmodule

module FULL_ADDER (
  input  Cin,
  input  A,
  input  B,
  output SUM,
  output Cout
);

  wire AND_2_out, AND_out, XOR_out;

  xor XOR (XOR_out, A, B);
  and AND (AND_out, A, B);
  xor XOR_2 (SUM, Cin, XOR_out);
  and AND_2 (AND_2_out, Cin, XOR_out);
  or OR (Cout, AND_2_out, AND_out);

  // Notes on the sheet:
  //   FULL ADDER
endmodule

module RIPPLE_CARRY_ADDER (
  input  Cin,
  input  [3:0] A,
  input  [3:0] B,
  output SUM0,
  output SUM1,
  output SUM2,
  output SUM3,
  output Cout
);

  wire FA0_cout, FA1_cout, FA2_cout;

  FULL_ADDER FA0 (.Cin(Cin), .A(A[0]), .B(B[0]), .SUM(SUM0), .Cout(FA0_cout));
  FULL_ADDER FA1 (.Cin(FA0_cout), .A(A[1]), .B(B[1]), .SUM(SUM1), .Cout(FA1_cout));
  FULL_ADDER FA2 (.Cin(FA1_cout), .A(A[2]), .B(B[2]), .SUM(SUM2), .Cout(FA2_cout));
  FULL_ADDER FA3 (.Cin(FA2_cout), .A(A[3]), .B(B[3]), .SUM(SUM3), .Cout(Cout));

  // Notes on the sheet:
  //   RIPPLE CARRY ADDER
  //   Cn
  //   Cn
  //   Cn
  //   CO
  //   C1
  //   C2
endmodule
