// Logisim project SHIFT_REGISTER.circ as structural Verilog: 3 circuits, main circuit SHIFT_RIGHT_REGISTER
module SHIFT_RIGHT_REGISTER (
  input  in_1
);

  wire clock_1_out, D0_q, D1_q, D2_q, D3_q;

  Clock clock_1 (.out(clock_1_out));
  LED led_1 (.in(D3_q));
  D_Flip_Flop D3 (.clk(clock_1_out), .D(in_1), .Q(D3_q));  // open: Qn, preset, en, reset
  D_Flip_Flop D2 (.clk(clock_1_out), .D(D3_q), .Q(D2_q));  // open: Qn, preset, en, reset
  LED led_2 (.in(D2_q));
  D_Flip_Flop D1 (.clk(clock_1_out), .D(D2_q), .Q(D1_q));  // open: Qn, preset, en, reset
  LED led_3 (.in(D1_q));
  LED led_4 (.in(D0_q));
  D_Flip_Flop D0 (.clk(clock_1_out), .D(D1_q), .Q(D0_q));  // open: Qn, preset, en, reset

  // Notes on the sheet:
  //   4 BIT SHIFT REGISTER (RIGHT SHIFT REGISTER)
endmodule

module SHIFT_LEFT_REGISTER (
  input  in_1
);

  wire clock_1_out, D0_q, D1_q, D2_q, D3_q;

  LED led_1 (.in(D3_q));
  D_Flip_Flop D3 (.clk(clock_1_out), .D(D2_q), .Q(D3_q));  // open: Qn, preset, en, reset
  D_Flip_Flop D2 (.clk(clock_1_out), .D(D1_q), .Q(D2_q));  // open: Qn, preset, en, reset
  LED led_2 (.in(D2_q));
  D_Flip_Flop D1 (.clk(clock_1_out), .D(D0_q), .Q(D1_q));  // open: Qn, preset, en, reset
  LED led_3 (.in(D1_q));
  LED led_4 (.in(D0_q));
  D_Flip_Flop D0 (.clk(clock_1_out), .D(in_1), .Q(D0_q));  // open: Qn, preset, en, reset
  Clock clock_1 (.out(clock_1_out));

  // Notes on the sheet:
  //   4 BIT SHIFT REGISTER (LEFT SHIFT REGISTER)
endmodule

module PIPO_SHIFT_REGISTER (
  input  in_1,
  input  in_2,
  input  in_3,
  input  in_4
);

  wire clock_1_out, D3_2_q, D3_3_q, D3_4_q, D3_q;

  Clock clock_1 (.out(clock_1_out));
  LED led_1 (.in(D3_q));
  D_Flip_Flop D3 (.clk(clock_1_out), .D(in_1), .Q(D3_q));  // open: Qn, preset, en, reset
  LED led_2 (.in(D3_2_q));
  D_Flip_Flop D3_2 (.clk(clock_1_out), .D(in_2), .Q(D3_2_q));  // open: Qn, preset, en, reset
  LED led_3 (.in(D3_3_q));
  D_Flip_Flop D3_3 (.clk(clock_1_out), .D(in_3), .Q(D3_3_q));  // open: Qn, preset, en, reset
  LED led_4 (.in(D3_4_q));
  D_Flip_Flop D3_4 (.clk(clock_1_out), .D(in_4), .Q(D3_4_q));  // open: Qn, preset, en, reset

  // Notes on the sheet:
  //   PARALEL_IN_PARALEL_OUT_SHIFT_REGISTER
endmodule
