// Logisim project ALU_Design.circ as structural Verilog
module ARITHEMATIC_UNIT_1_BIT (
  input  in_1,
  input  in_2,
  input  in_3,
  input  [1:0] in_4,
  output out_5,
  output out_6
);

  wire multiplexer_1_out, multiplexer_2_out, not_1_out, not_2_out, not_3_out;

  not not_1 (not_1_out, in_3);
  not not_2 (not_2_out, 1'b1);
  Multiplexer #(.select(2), .enable("false")) multiplexer_1 (
    .in0(in_3), .in1(not_1_out), .in2(1'b1), .in3(not_2_out), .out(multiplexer_1_out), .sel(in_4));
  Multiplexer #(.enable("false")) multiplexer_2 (
    .in0(multiplexer_1_out), .in1(not_3_out), .out(multiplexer_2_out), .sel(in_1));
  not not_3 (not_3_out, multiplexer_1_out);
  Adder #(.width(1)) adder_1 (.a(in_2), .b(multiplexer_2_out), .out(out_5), .cin(in_1), .cout(out_6));
endmodule

module LOGICAL_UNIT_1_BIT (
  input  in_1,
  input  in_2,
  input  [2:0] in_3,
  output out_4
);

  wire and_1_out, not_1_out, not_2_out, or_1_out, xor_1_out;

  and and_1 (and_1_out, in_1, in_2);
  or or_1 (or_1_out, in_1, in_2);
  not not_1 (not_1_out, in_1);
  not not_2 (not_2_out, in_2);
  xor xor_1 (xor_1_out, in_1, in_2);
  Multiplexer #(.select(3), .enable("false")) multiplexer_1 (
    .in0(or_1_out), .in1(and_1_out), .in2(xor_1_out), .in3(not_1_out), .in4(not_2_out), .out(out_4),
    .sel(in_3));  // open: in5, in6, in7
endmodule
